# Fritzing sketch wallbot with screen-wiring-nr (saved by Fritzing 0.9.6b)
circuit board: 7.4cm x 4.4cm

parts:
  File = Toggle Switch [package=THT]
  m1 = double row female pin header, 16 pins [form="♀ (female)"]
  SD = female pin header, 6 pins [form="♀ (female)"]
  LED = female pin header, 3 pins [form="♀ (female)"]
  CS4 = SWITCH-MOMENTARY-2 [package=tactile_switch_smd-2]
  CS5 = SWITCH-MOMENTARY-2 [package=tactile_switch_smd-2]
  CS6 = SWITCH-MOMENTARY-2 [package=tactile_switch_smd-2]
  UNLOAD = SWITCH-MOMENTARY-2 [package=tactile_switch_smd-2]
  LOAD = SWITCH-MOMENTARY-2 [package=tactile_switch_smd-2]
  CM = Toggle Switch [package=THT]
  5V = female pin header, 2 pins [form="♀ (female)"]

nets:
  N1: File.COM, m1.pin1, SD.pin6, LED.pin1, CS4.1, CS5.1, CS6.1, UNLOAD.1, LOAD.1, CM.COM, 5V.pin1
  N2: File.L2, m1.pin5
  N3: m1.pin2, SD.pin1
  N4: m1.pin3, SD.pin3
  N5: m1.pin4, LED.pin3
  N6: m1.pin6, CM.L2
  N7: m1.pin7, CS6.2
  N8: m1.pin10, CS5.2
  N9: m1.pin11, CS4.2
  N10: m1.pin12, UNLOAD.2
  N11: m1.pin13, LOAD.2
  N12: m1.pin14, SD.pin4
  N13: m1.pin15, SD.pin2
  N14: SD.pin5, LED.pin2, 5V.pin2

notes:
  Robuc WallBot v1
  Team 4160
  Inter
  File
  Gc
  D
  - + Mi Mo S C
  D + -
  5V + -
  G
